// Logisim project CLA.circ as structural Verilog: 2 circuits, main circuit main
module carry_block (
  input  Cin,
  input  [3:0] A,
  input  [3:0] B,
  output [3:0] sum,
  output Cout
);

  wire and_1_out, and_4_out, and_5_out, and_7_out, and_8_out, and_10_out, G0, G1, G2, G3, or_5_out, or_7_out,
       or_8_out, or_9_out, P0, P1, P2, P3;

  and and_1 (and_1_out, P3, P2, P1, P2);
  or or_1 (P3, B[3], A[3]);
  and and_2 (G3, B[3], A[3]);
  or or_2 (P2, B[2], A[2]);
  and and_3 (G2, B[2], A[2]);
  and and_4 (and_4_out, and_1_out, Cin);
  or or_3 (Cout, and_4_out, or_5_out);
  or or_4 (P1, B[1], A[1]);
  and and_5 (and_5_out, P3, or_8_out);
  or or_5 (or_5_out, G3, and_5_out);
  and and_6 (G1, B[1], A[1]);
  or or_6 (P0, B[0], A[0]);
  and and_7 (and_7_out, G0, P1);
  or or_7 (or_7_out, G1, and_7_out);
  and and_8 (and_8_out, P2, or_7_out);
  or or_8 (or_8_out, G2, and_8_out);
  and and_9 (G0, B[0], A[0]);
  and and_10 (and_10_out, P0, Cin);
  or or_9 (or_9_out, G0, and_10_out);
  ExactlyOne xor_1 (.out(sum[3]), .in0(B[3]), .in1(or_8_out), .in2(A[3]));
  ExactlyOne xor_2 (.out(sum[2]), .in0(B[2]), .in1(or_7_out), .in2(A[2]));
  ExactlyOne xor_3 (.out(sum[1]), .in0(B[1]), .in1(or_9_out), .in2(A[1]));
  ExactlyOne xor_4 (.out(sum[0]), .in0(B[0]), .in1(Cin), .in2(A[0]));

  // Other names for the same wires on the sheet: S0 = sum[0]; S1 = sum[1]; S2 = sum[2]; S3 = sum[3]
endmodule

module main (
  input  [3:0] A,
  input  [3:0] B,
  output [3:0] Sum,
  output Cout
);

  carry_block carry_block_1 (.Cin(1'b0), .A(A), .B(B), .sum(Sum), .Cout(Cout));
endmodule
